# Fritzing sketch Schematic (saved by Fritzing 1.0.4)
breadboards: 1

parts:
  A1 = ESP32-S3 zero
  C1 = Electrolytic Capacitor [capacitance=1µF voltage=35V package="100 mil [THT, electrolytic]"]
  U1 = WS2812 RGB LED strip [mn=60]
  U3 = 74x125 [part_number=74HCT125 package="DIP (Dual Inline) [THT]"]
  part = 74x125 [part_number=74HCT125 package="DIP (Dual Inline) [THT]"]
  U3_1 = 74x125 [part_number=74x125 package="DIP (Dual Inline) [THT]"]
  U3_2 = 74x125 [part_number=74x125 package="DIP (Dual Inline) [THT]"]  # not connected
  U3_3 = 74x125 [part_number=74x125 package="DIP (Dual Inline) [THT]"]  # not connected
  U3_4 = 74x125 [part_number=74x125 package="DIP (Dual Inline) [THT]"]  # not connected
  C2 = Ceramic Capacitor [capacitance=100nF voltage=35V package="100 mil [THT, multilayer]"]

nets:
  5V: A1.Pin_1, C1.+, U1.VCC, U3.connector13, part.VCC, C2.1
  GND: A1.Pin_2, C1.-, U1.GND, U3.connector0, U3.connector6, part.GND, U3_1.C1, C2.0
  N1: A1.Pin_4, U3.connector1, U3_1.A1
  N2: U1.DIN, U3.connector2, U3_1.Y1

notes:
  ESP32-S3-zero board with level-shift (3.3V to 5V) on LED dataline.
  Additional capacity to support 5V rail to LEDs.
  WS2812b LED strip
  60 LEDs

custom parts:
  ESP32-S3 zero: ESP32-S3 Mini Development Board, Based on ESP32-S3FH4R2 Dual-Core Processor, 240MHz Running Frequency, 2.4GHz Wi-Fi & Bluetooth 5.
  WS2812 RGB LED strip: WS2812 strip
  74x125: 74x125 quad tristate buffer active low enable. The 74ahc125 variety is useful as a level translator as the inputs are 5V tolorant when run with a VCC of 3.3V (and will thus take a 5V signal in and provide a 3.3V signal out.) As well this part uses schematic subparts so you can drag each of the 4 gates to a different place in schematic view. Note having many (around 10 or more) subpart parts in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
  74x125: 74x125 quad tristate buffer active low enable. The 74ahc125 variety is useful as a level translator as the inputs are 5V tolorant when run with a VCC of 3.3V (and will thus take a 5V signal in and provide a 3.3V signal out.) As well this part uses schematic subparts so you can drag each of the 4 gates to a different place in schematic view. Note having many (around 10 or more) subpart parts in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
  74x125: 74x125 quad tristate buffer active low enable. The 74ahc125 variety is useful as a level translator as the inputs are 5V tolorant when run with a VCC of 3.3V (and will thus take a 5V signal in and provide a 3.3V signal out.) As well this part uses schematic subparts so you can drag each of the 4 gates to a different place in schematic view. Note having many (around 10 or more) subpart parts in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
  74x125: 74x125 quad tristate buffer active low enable. The 74ahc125 variety is useful as a level translator as the inputs are 5V tolorant when run with a VCC of 3.3V (and will thus take a 5V signal in and provide a 3.3V signal out.) As well this part uses schematic subparts so you can drag each of the 4 gates to a different place in schematic view. Note having many (around 10 or more) subpart parts in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
  74x125: 74x125 quad tristate buffer active low enable. The 74ahc125 variety is useful as a level translator as the inputs are 5V tolorant when run with a VCC of 3.3V (and will thus take a 5V signal in and provide a 3.3V signal out.) As well this part uses schematic subparts so you can drag each of the 4 gates to a different place in schematic view. Note having many (around 10 or more) subpart parts in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
  74x125: 74x125 quad tristate buffer active low enable. The 74ahc125 variety is useful as a level translator as the inputs are 5V tolorant when run with a VCC of 3.3V (and will thus take a 5V signal in and provide a 3.3V signal out.) As well this part uses schematic subparts so you can drag each of the 4 gates to a different place in schematic view. Note having many (around 10 or more) subpart parts in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
